# Fritzing sketch PCB_FINAL (saved by Fritzing 0.9.3b)
circuit board: 6.31109cm x 6.03909cm
breadboards: 1

parts:
  R1_220Ω = Resistor [tolerance=±5% resistance=220 package=THT]
  R2_220Ω = Resistor [tolerance=±5% resistance=220 package=THT]
  R4_220Ω = Resistor [tolerance=±5% resistance=220 package=THT]
  R5_220Ω = Resistor [tolerance=±5% resistance=220 package=THT]
  R3_220Ω = Resistor [tolerance=±5% resistance=220 package=THT]
  R6_1KΩ = Resistor [tolerance=±5% resistance=1k package=THT]
  PIN1 = Header 1 [package=smtso-256-et]
  PIN2 = Header 1 [package=smtso-256-et]
  PIN3 = Header 1 [package=smtso-256-et]
  PIN4 = Header 1 [package=smtso-256-et]
  PIN5 = Header 1 [package=smtso-256-et]
  LDR_vIN = Header 1 [package=smtso-256-et]
  L1_IN = Header 1 [package=smtso-256-et]
  L2_IN = Header 1 [package=smtso-256-et]
  L3_IN = Header 1 [package=smtso-256-et]
  L4_IN = Header 1 [package=smtso-256-et]
  L5_IN = Header 1 [package=smtso-256-et]
  PIN9 = Header 1 [package=smtso-256-et]
  L1_OUT = Header 1 [package=smtso-256-et]
  L2_OUT = Header 1 [package=smtso-256-et]
  L3_OUT = Header 1 [package=smtso-256-et]
  L4_OUT = Header 1 [package=smtso-256-et]
  L5_OUT = Header 1 [package=smtso-256-et]
  GND = Header 1 [package=smtso-256-et]

nets:
  N1: R1_220Ω.Pin_0, PIN1.1
  N2: R1_220Ω.Pin_1, L1_IN.1
  N3: R2_220Ω.Pin_0, PIN2.1
  N4: R2_220Ω.Pin_1, L2_IN.1
  N5: R4_220Ω.Pin_0, PIN4.1
  N6: R4_220Ω.Pin_1, L4_IN.1
  N7: R5_220Ω.Pin_0, PIN5.1
  N8: R5_220Ω.Pin_1, L5_IN.1
  N9: R3_220Ω.Pin_0, PIN3.1
  N10: R3_220Ω.Pin_1, L3_IN.1
  N11: R6_1KΩ.Pin_0, LDR_vIN.1, PIN9.1
  N12: R6_1KΩ.Pin_1, L1_OUT.1, L2_OUT.1, L3_OUT.1, L4_OUT.1, L5_OUT.1, GND.1
